# Fritzing sketch CySafety (saved by Fritzing 0.9.3b)
circuit board: 16.6194cm x 9.35633cm
breadboards: 2

parts:
  IC1 = Voltage Regulator [package=to-220-alt]
  C2 = Electrolytic Capacitor [capacitance=0.1µF package="200 mil [THT, electrolytic]"]
  C3 = Electrolytic Capacitor [capacitance=0.22mF voltage=10V package="200 mil [THT, electrolytic]"]
  S1 = SPST Switch [package=switch-spdt]
  LED1 = LED - 5mm [color="Red (633nm)" package="5 mm [THT]"]
  R1 = Resistor [tolerance=±5% resistance=150 package=THT]
  J1 = Screw terminal - 2 pins [package=THT]
  MQ2 = Gas Sensor Breakout Board
  R2 = Resistor [tolerance=±5% resistance=2.2k package=THT]
  R3 = Resistor [tolerance=±5% resistance=3.3k package=THT]
  U1 = POT [package=trim_pot]
  R4 = Photocell (LDR) [package=THT]
  LED2 = LED - 5mm [color="Green (565nm)" package="5 mm [THT]"]
  J2 = male pin header, 2 pins [form="♂ (male)"]
  J3 = male pin header, 6 pins [form="♂ (male)"]
  ADS1115 = Adafruit ADS1115 16Bit I2C ADC [part_number="Adafruit #1085"]
  J4 = male pin header, 3 pins [form="♂ (male)"]
  J5 = male pin header, 3 pins [form="♂ (male)"]
  J6 = male pin header, 6 pins [form="♂ (male)"]
  Huzzah_ESP8266 = Adafruit HUZZAH ESP8266 [part_number="Adafruit #2471"]
  BME280 = Adafruit BME280

nets:
  GND: IC1.GND, C2.-, C3.-, R1.Pin_0, J1.pin1, MQ2.GND, R3.Pin_1, U1.A, LED2.cathode, J3.pin1, ADS1115.GND, J4.pin3, Huzzah_ESP8266.GND, BME280.GND
  N1: IC1.IN, C3.+, S1.S
  N2: IC1.OUT, C2.+, LED1.anode, MQ2.A1, MQ2.H1, J3.pin3, J4.pin1, Huzzah_ESP8266.VIN
  N3: S1.P, J1.pin2
  N4: LED1.cathode, R1.Pin_1
  N5: MQ2.B1, R2.Pin_1, R3.Pin_0
  N6: R2.Pin_0, Huzzah_ESP8266.ADC
  N7: U1.S, R4.pin_1, ADS1115.AIN0
  VDD: R4.pin_0, ADS1115.VDD, J4.pin2, Huzzah_ESP8266.3.3V, BME280.VIN
  N8: LED2.anode, Huzzah_ESP8266.GPIO5
  N9: J2.pin1, ADS1115.SCL, Huzzah_ESP8266.GPIO0, BME280.SCK/SCL
  N10: J2.pin2, ADS1115.ADDR, ADS1115.SDA, Huzzah_ESP8266.GPIO4, BME280.SDI/SDA
  N11: J3.pin4, Huzzah_ESP8266.RX
  N12: J3.pin5, Huzzah_ESP8266.TX
  N13: ADS1115.AIN3, J5.pin3
  N14: ADS1115.AIN2, J5.pin2
  N15: ADS1115.AIN1, J5.pin1
  N16: J6.pin1, Huzzah_ESP8266.GPIO13
  N17: J6.pin2, Huzzah_ESP8266.GPIO12
  N18: J6.pin3, Huzzah_ESP8266.GPIO14
  N19: J6.pin4, Huzzah_ESP8266.GPIO16
  N20: J6.pin5, Huzzah_ESP8266.GPIO15
  N21: J6.pin6, Huzzah_ESP8266.GPIO2

notes:
  CySafety, WiFi IoT Home Safety Monitor, 1.1
  SCL
  SDA
  D13
  D12
  D14
  D16
  D15
  D2
  5V
  3.3V
  GND
  A1
  A2
  A3
  RX
  TX
  9VDC IN
  +
  -
  Heartbeat
  PWR
  ON / OFF
  CySafety Rev 1.1
  Copyright (c) 2020 Cyrus Brunner
  www.cyrusbuilt.net
  FAB 00100 ASSY 001002
  IoT WiFi Safety Monitor
  1.5A MAX
  LDR Trim

custom parts:
  Adafruit ADS1115 16Bit I2C ADC: For microcontrollers without an analog-to-digital converter or when you want a higher-precision ADC, the ADS1115 provides 16-bit precision at 860 samples/second over I2C. The chip can be configured as 4 single-ended input channels, or two differential channels. As a nice bonus, it even includes a programmable gain amplifier, up to x16, to help boost up smaller single/differential signals to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
  Adafruit HUZZAH ESP8266: Add Internet to your next project with an adorable, bite-sized WiFi microcontroller, at a price you like! The ESP8266 processor from Espressif is an 80 MHz microcontroller with a full WiFi front-end (both as client and access point) and TCP/IP stack with DNS support as well. While this chip has been very popular, its also been very difficult to use. Most of the low cost modules are not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
  Adafruit BME280: Bosch has stepped up their game with their new BME280 sensor, an environmental sensor with temperature, barometric pressure and humidity! This sensor is great for all sorts of weather/environmental sensing and can even be used in both I2C and SPI! This precision sensor from Bosch is the best low-cost sensing solution for measuring humidity with ±3% accuracy, barometric pressure with ±1 hPa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
